# Fritzing sketch boost-gauge (saved by Fritzing 0.9.3b)
breadboards: 1

parts:
  BeagleBone1 = BeagleBone Black
  Part1 = OLED Color 1.5 inch 128x128 w microSD [part_number=1431]
  Part2 = 24 NeoPixel Ring [part_number=1586]
  Part3 = SOIC-14 [chip_label=CAN part_number=SN65HVD230 package=SO]

nets:
  GND: BeagleBone1.no_name_yet#1, Part1.GND, Part2.GND, Part3.2
  N1: BeagleBone1.no_name_yet#3, Part2.VDD, Part3.1
  N2: BeagleBone1.no_name_yet#7, Part1.VIN
  N3: BeagleBone1.no_name_yet#15, Part1.RESET
  N4: BeagleBone1.no_name_yet#22, Part2.IN
  N5: BeagleBone1.no_name_yet#23, Part1.DC
  N6: BeagleBone1.no_name_yet#24, Part3.4
  N7: BeagleBone1.no_name_yet#26, Part3.3
  N8: BeagleBone1.no_name_yet#28, Part1.OLED_CS
  N9: BeagleBone1.no_name_yet#30, Part1.MOSI
  N10: BeagleBone1.no_name_yet#31, Part1.SCK

notes:
  car CAN high
  car CAN low

custom parts:
  BeagleBone Black: BeagleBone Black rev. A5B
  OLED Color 1.5 inch 128x128 w microSD: The visible portion of this OLED measures 1.5" diagonal and contains 128x128 RGB pixels, each one made of red, green and blue OLEDs. Each pixel can be set with 16-bits of resolution for a large range of colors. Because the display uses OLEDs, there is no backlight, and the contrast is very high (black is really black). We picked this display for its excellent color, this is the nicest mini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
  24 NeoPixel Ring: 24 ultra bright smart LED NeoPixels are arranged in a circle with 2.6" (66mm) outer diameter. The rings are 'chainable' - connect the output pin of one to the input pin of another. Use only one microcontroller pin to control as many as you can chain together! Each LED is addressable as the driver chip is inside the LED. Each one has ~18mA constant current drive so the color will be very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
